# Fritzing sketch Di2c03 (saved by Fritzing 0.9.3b)
circuit board: 5.34cm x 2.96357cm
breadboards: 1

parts:
  R4 = Resistor [tolerance=±5% resistance=100 package="2010 [SMD]"]
  R5 = Resistor [tolerance=±5% resistance=680 package="2010 [SMD]"]
  R7 = Resistor [tolerance=±5% resistance=100 package="2010 [SMD]"]
  C2 = Ceramic Capacitor [capacitance=100nF package="0603 [SMD, multilayer]"]
  R3 = Resistor [tolerance=±5% resistance=680 package="2010 [SMD]"]
  J3 = male pin header, 9 pins [form="♂ (male)"]
  R1 = Resistor [tolerance=±5% resistance=2.2k package="2010 [SMD]"]
  R8 = Resistor [tolerance=±5% resistance=680 package="2010 [SMD]"]
  J2 = male pin header, 8 pins [form="♂ (male)"]
  R6 = Resistor [tolerance=±5% resistance=680 package="2010 [SMD]"]
  J4 = male pin header, 4 pins [form="♂ (male)"]
  C1 = Ceramic Capacitor [capacitance=100nF package="0603 [SMD, multilayer]"]
  R2 = Resistor [tolerance=±5% resistance=2.2k package="2010 [SMD]"]
  Pad1 = Pad [width=0.20000000000000001 height=2 connect=center]
  Pad2 = Pad [width=0.20000000000000001 height=2 connect=center]
  Pad3 = Pad [width=0.20000000000000001 height=2 connect=center]
  Pad4 = Pad [width=0.20000000000000001 height=2 connect=center]
  Pad5 = Pad [width=0.20000000000000001 height=2 connect=center]
  Pad6 = Pad [width=0.20000000000000001 height=2 connect=center]
  Pad7 = Pad [width=0.20000000000000001 height=2 connect=north]
  Pad8 = Pad [width=0.20000000000000001 height=2 connect=center]
  Pad9 = Pad [width=0.20000000000000001 height=2 connect=south]
  Pad10 = Pad [width=0.20000000000000001 height=2 connect=center]

nets:
  N1: R4.Pin_0, R5.Pin_1, J3.pin6, J2.pin6, Pad1.pad
  N2: R4.Pin_1, R3.Pin_0, J3.pin5, J2.pin5, Pad2.pad
  N3: R5.Pin_0, C2.1, J3.pin4, J2.pin4, R6.Pin_0, J4.pin2, J4.pin4, C1.1, Pad10.pad
  N4: R7.Pin_0, J3.pin8, J2.pin8, R6.Pin_1, Pad4.pad
  N5: R7.Pin_1, J3.pin7, R8.Pin_0, J2.pin7, Pad6.pad
  N6: C2.0, R1.Pin_1, J4.pin3, R2.Pin_0, Pad5.pad
  N7: R3.Pin_1, J3.pin3, R8.Pin_1, J2.pin3, J4.pin1, C1.0, Pad3.pad
  N8: J3.pin1, J2.pin1, R2.Pin_1, Pad9.pad
  N9: J3.pin2, R1.Pin_0, J2.pin2, Pad7.pad
  N10: J3.pin9, Pad8.pad

notes:
  DI2C
  SCL
  SDA
  V(B)
  V(A)
  GND
  DSDAP
  DSDAM
  DSCLP
  DSCLM
  EN
  + 3,3 V / 5 V
  + 5 V
