# Fritzing sketch universal_slave (saved by Fritzing 0.9.3b)
circuit board: 10.4cm x 3.8cm
breadboards: 1

parts:
  Part1 = Arduino Nano (Rev3.0)
  J1 = female pin header, 8 pins [form="♀ (female)"]
  J2 = female pin header, 11 pins [form="♀ (female)"]
  J3 = female pin header, 4 pins [form="♀ (female)"]
  C1 = Electrolytic Capacitor [capacitance=0.1mF package="100 mil [THT, electrolytic]"]
  J4 = female pin header, 5 pins [form="♀ (female)"]
  J5 = female pin header, 5 pins [form="♀ (female)"]
  J6 = female pin header, 5 pins [form="♀ (female)"]
  J7 = female pin header, 5 pins [form="♀ (female)"]
  J8 = female pin header, 4 pins [form="♀ (female)"]
  J9 = female pin header, 3 pins [form="♀ (female)"]
  J10 = female pin header, 3 pins [form="♀ (female)"]
  U1 = Voltage Regulator - 5V [package="TO220 [THT]"]
  C2 = Ceramic Capacitor [capacitance=100nF package="100 mil [THT, multilayer]"]
  C3 = Tantalum Capacitor [capacitance=1μF package="100 mil [THT, tantalum]"]
  J12 = Screw terminal - 2 pins [package=THT]
  J11 = Screw terminal - 2 pins [package=THT]
  C4 = Ceramic Capacitor [capacitance=100nF package="100 mil [THT, multilayer]"]
  R1 = Resistor [tolerance=±5% resistance=10k package=THT]
  R2 = Resistor [tolerance=±5% resistance=10k package=THT]
  C5 = Ceramic Capacitor [capacitance=100nF package="100 mil [THT, multilayer]"]
  J13 = female pin header, 2 pins [form="♀ (female)"]
  J14 = female pin header, 11 pins [form="♀ (female)"]
  R3 = Resistor [tolerance=±5% resistance=4.7k package=THT]
  R4 = Resistor [tolerance=±5% resistance=4.7k package=THT]
  R5 = Resistor [tolerance=±5% resistance=4.7k package=THT]
  R6 = Resistor [tolerance=±5% resistance=4.7k package=THT]
  J15 = female pin header, 4 pins [form="♀ (female)"]
  Pololu_A1 = Pololu A4988 [package=SO16]

nets:
  GND: Part1.GND, C1.-, J4.pin1, J4.pin2, J4.pin3, J4.pin4, J4.pin5, J6.pin1, J6.pin2, J6.pin3, J6.pin4, J6.pin5, U1.GND, C2.1, C3.-, J11.pin2, C4.0, R1.Pin_0, R2.Pin_0, C5.0, Pololu_A1.GND
  N1: Part1.D2, J2.pin1, J14.pin1, Pololu_A1.DIR
  N2: Part1.D3, J2.pin2, J14.pin2, Pololu_A1.STEP
  N3: Part1.D4, J2.pin3, J14.pin3
  N4: Part1.D5, J2.pin4, J14.pin4
  N5: Part1.D6, J2.pin5, J14.pin5
  N6: Part1.D7, J2.pin6, J14.pin6
  N7: Part1.D8, J2.pin7, J14.pin7
  N8: Part1.D9, J2.pin8, J14.pin8
  N9: Part1.D10, J2.pin9, J14.pin9
  N10: Part1.D11/MOSI, J2.pin10, J14.pin10
  N11: Part1.D12/MISO, J2.pin11, J14.pin11
  5V: Part1.5V, J7.pin1, J7.pin2, J7.pin3, J7.pin4, J7.pin5, J10.pin1, J10.pin2, J10.pin3, U1.output_voltage, C2.0, R3.Pin_0, R4.Pin_0, R5.Pin_0, R6.Pin_0, Pololu_A1.RESET, Pololu_A1.SLEEP, Pololu_A1.VDD
  N12: Part1.A7, J1.pin1
  N13: Part1.A6, J1.pin2
  N14: Part1.A5, J1.pin3, J12.pin1
  N15: Part1.A4, J1.pin4, J12.pin2
  N16: Part1.A3, J1.pin5
  N17: Part1.A2, J1.pin6
  N18: Part1.A1, J1.pin7
  N19: Part1.A0, J1.pin8
  N20: J3.pin1, J8.pin1, Pololu_A1.2B
  N21: J3.pin2, J8.pin2, Pololu_A1.2A
  N22: J3.pin3, J8.pin3, Pololu_A1.1A
  N23: J3.pin4, J8.pin4, Pololu_A1.1B
  N24: C1.+, J5.pin1, J5.pin2, J5.pin3, J5.pin4, J5.pin5, U1.input_voltage, C3.+, J11.pin1, Pololu_A1.VMOT
  N25: J9.pin1, Pololu_A1.MS1
  N26: J9.pin2, Pololu_A1.MS2
  N27: J9.pin3, Pololu_A1.MS3
  N28: C4.1, R1.Pin_1, J13.pin1
  N29: R2.Pin_1, C5.1, J13.pin2
  N30: R3.Pin_1, J15.pin1
  N31: R4.Pin_1, J15.pin2
  N32: R5.Pin_1, J15.pin3
  N33: R6.Pin_1, J15.pin4

notes:
  12V
  I2C
  DRV 8825
  Arduino Nano
  stepmotor
  stepsetting
  pull up
  GND
  + 12 V
  + 5 V
  prell
  analog I/O
  digital I/O
