# Fritzing sketch Omstyring (saved by Fritzing 0.9.0b)
breadboards: 1

parts:
  Part1 = Arduino Nano (Rev3.0)
  U1 = Voltage Regulator - 5V [package="TO220 [THT]"]
  C1 = Tantalum Capacitor [capacitance=1μF package="100 mil [THT, tantalum]"]
  C2 = Ceramic Capacitor [capacitance=1µF package="100 mil [THT, multilayer]"]
  J1 = Screw terminal - 2 pins [package=THT]
  R1 = Slide Potentiometer [maximum_resistance=100kΩ]
  S1 = Toggle Switch [package=THT]
  C3 = Ceramic Capacitor [capacitance=100nF package="100 mil [THT, multilayer]"]
  R2 = Resistor [tolerance=±5% resistance=10k package=THT]
  DRV_1 = DRV 8825 Stepper Motor Carrier, High Current [part_number="DRV 8825"]
  C4 = Electrolytic Capacitor [capacitance=0.1mF package="100 mil [THT, electrolytic]"]
  M1 = Stepper Motor - Bipolar  # not connected

nets:
  GND: Part1.GND, U1.GND, C1.+, C2.0, R1.leg2, C3.0, R2.Pin_0, DRV_1.GROUND_LOG, C4.-
  N1: Part1.D4, S1.COM, C3.1, R2.Pin_1
  N2: Part1.5V, U1.output_voltage, C2.1, R1.leg1, S1.L1
  N3: Part1.A5, J1.pin1
  N4: Part1.A4, J1.pin2
  N5: Part1.A1, R1.wiper
  N6: U1.input_voltage, C1.-, C4.+

notes:
  + 12 V
  GND
  +5 V
  I2C
