# Fritzing sketch model computer ver2 (saved by Fritzing 0.9.3b)
circuit board: 10cm x 8cm
breadboards: 2

parts:
  Part1 = Arduino Nano (Rev3.0)
  C1 = Electrolytic Capacitor [capacitance=0.1mF voltage=16V package="100 mil [THT, electrolytic]"]
  Q1 = NPN-Transistor [package="TO92 [THT]"]
  Q2 = Basic FET N-Channel [package="TO220 [THT]"]
  R4 = Resistor [tolerance=±5% resistance=220 package=THT]
  R5 = Resistor [tolerance=±5% resistance=220 package=THT]
  Q3 = NPN-Transistor [package="TO92 [THT]"]
  Q4 = Basic FET N-Channel [package="TO220 [THT]"]
  R6 = Resistor [tolerance=±5% resistance=220 package=THT]
  R7 = Resistor [tolerance=±5% resistance=220 package=THT]
  Q5 = NPN-Transistor [package="TO92 [THT]"]
  Q6 = Basic FET N-Channel [package="TO220 [THT]"]
  R8 = Resistor [tolerance=±5% resistance=220 package=THT]
  R9 = Resistor [tolerance=±5% resistance=220 package=THT]
  Q7 = NPN-Transistor [package="TO92 [THT]"]
  Q8 = Basic FET N-Channel [package="TO220 [THT]"]
  R10 = Resistor [tolerance=±5% resistance=220 package=THT]
  R11 = Resistor [tolerance=±5% resistance=220 package=THT]
  R12 = Resistor [tolerance=±5% resistance=220 package=THT]
  R13 = Resistor [tolerance=±5% resistance=220 package=THT]
  R14 = Resistor [tolerance=±5% resistance=10k package=THT]
  R15 = Resistor [tolerance=±5% resistance=10k package=THT]
  C2 = Ceramic Capacitor [capacitance=100nF package="100 mil [THT, multilayer]"]
  C3 = Ceramic Capacitor [capacitance=100nF package="100 mil [THT, multilayer]"]
  J13 = Screw terminal - 2 pins [package=THT]
  J12 = Screw terminal - 2 pins [package=THT]
  J4 = Screw terminal - 2 pins [package=THT]
  J5 = Screw terminal - 2 pins [package=THT]
  J6 = Screw terminal - 2 pins [package=THT]
  J7 = Screw terminal - 2 pins [package=THT]
  J3 = Screw terminal - 2 pins [package=THT]
  J2 = Screw terminal - 2 pins [package=THT]
  J1 = Screw terminal - 2 pins [package=THT]
  J14 = Screw terminal - 2 pins [package=THT]
  J11 = Screw terminal - 2 pins [package=THT]
  J10 = Screw terminal - 2 pins [package=THT]
  J8 = Screw terminal - 2 pins [package=THT]
  J9 = Screw terminal - 2 pins [package=THT]

nets:
  GND: Part1.GND, C1.-, Q1.E, R5.Pin_1, Q3.E, R7.Pin_1, Q5.E, R9.Pin_1, Q7.E, R11.Pin_1, J2.pin1, J1.pin1, J14.pin1, J14.pin2, J11.pin2, J10.pin2
  N1: Part1.D2, R13.Pin_1
  N2: Part1.D3, R15.Pin_0, C3.0, J9.pin2
  N3: Part1.D4, R14.Pin_0, C2.0, J8.pin2
  N4: Part1.D5, R4.Pin_1
  N5: Part1.D6, R6.Pin_1
  N6: Part1.D7, J13.pin1
  N7: Part1.D8, J13.pin2
  N8: Part1.D9, R8.Pin_1
  N9: Part1.D10, R10.Pin_1
  N10: Part1.D11/MOSI, J12.pin2
  N11: Part1.D12/MISO, J12.pin1
  N12: Part1.VIN, J1.pin2, J8.pin1, J9.pin1
  N13: Part1.A5, J3.pin1
  N14: Part1.A4, J3.pin2
  N15: Part1.A0, R12.Pin_1
  N16: C1.+, J4.pin1, J5.pin1, J6.pin1, J7.pin1, J2.pin2
  N17: Q1.B, Q2.source, R5.Pin_0
  N18: Q1.C, Q2.gate, R4.Pin_0
  N19: Q2.drain, J4.pin2
  N20: Q3.B, Q4.source, R7.Pin_0
  N21: Q3.C, Q4.gate, R6.Pin_0
  N22: Q4.drain, J5.pin2
  N23: Q5.B, Q6.source, R9.Pin_0
  N24: Q5.C, Q6.gate, R8.Pin_0
  N25: Q6.drain, J6.pin2
  N26: Q7.B, Q8.source, R11.Pin_0
  N27: Q7.C, Q8.gate, R10.Pin_0
  N28: Q8.drain, J7.pin2
  N29: R12.Pin_0, J11.pin1
  N30: R13.Pin_0, J10.pin1
  N31: R14.Pin_1, R15.Pin_1, C2.1, C3.1

notes:
  + 5 V
  0 V
  + 12 V
  lys HT top
  lys HT bund
  lys LT top
  lys LT bund
  microswitch omstyring venstre
  microswitch omstyring højre
  IR diode hovedaksel
  IR sensor hovedaksel
  GND
  LED LT bund
  LED LT top
  LED HT bund
  LED HT top
  R4-R11 skal beregnes når effekten af de fire Power LEDs kendes.
  Microswitch omstyring højre
  Microswitch omstyring venstre
  ARDUINO
  A0: IR detector til 0-stilling af hovedmotor
  A4: I2C SDA
  A5: I2C SCL
  D2: IR emitter til 0-stilling af hovedmotor
  D3: Microswitch omstyring højre
  D4: Microswitch omstyring venstre
  D5: Lys HT bund
  D6: Lys LT top
  D7: Styring af omløbsretning på motor 2 (CW+)
  D8: Stepsignal til motor 2 (CLK+)
  D9: Lys HT bund
  D10: Lys HT top
  D11: Styring af omløbsretning på motor 1 (CW+)
  D12: Stepsignal til motor 1 (CLK+)
  TB 6560 Driver input
  Driver Motor 1:
  CLK+: forbindes til D12
  CLK-: forbindes til GND
  CW+: forbindes til D11
  CW-: forbindes til GND
  EN+: forbindes ikke
  EN-: forbindes ikke
  Driver Motor 2:
  CLK+: forbindes til D8
  CLK-: forbindes til GND
  CW+: forbindes til D7
  CW-: forbindes til GND
  EN+: forbindes ikke
  EN-: forbindes ikke
  TB 6560 Driver output
  Driver motor 1 = motor 2:
  +24V: forbindes til 24 V strømforsyning
  GND: forbindes til fælles GND
  A+: forbindes til sort motorkabel
  A-: forbindes til grønt motorkabel
  B+: forbindes til rødt motorkabel
  B-: forbindes til blåt motorkabel
  CLK+ (1)
  CW+ (1)
  CLK+ (2)
  CW+ (2)
  I2C SDA
  I2C SCL
  pin:C
  pin: C
  pin: NC
