# Fritzing sketch programvalg slave (saved by Fritzing 0.9.3b)
circuit board: 10.5cm x 3.84469cm
breadboards: 1

parts:
  Part1 = Arduino Nano (Rev3.0)
  U1 = Voltage Regulator - 5V [package="TO220 [THT]"]
  C1 = Tantalum Capacitor [capacitance=1μF package="100 mil [THT, tantalum]"]
  C2 = Ceramic Capacitor [capacitance=100nF package="100 mil [THT, multilayer]"]
  R1 = Resistor [tolerance=±5% resistance=10k package=THT]
  R2 = Resistor [tolerance=±5% resistance=10k package=THT]
  R3 = Resistor [tolerance=±5% resistance=10k package=THT]
  R4 = Resistor [tolerance=±5% resistance=10k package=THT]
  R5 = Resistor [tolerance=±5% resistance=47k package=THT]
  D1 = Rectifier Diode [part_number=1N4001 package="300 mil [THT]"]
  D2 = Rectifier Diode [part_number=1N4001 package="300 mil [THT]"]
  D3 = Rectifier Diode [part_number=1N4001 package="300 mil [THT]"]
  D4 = Rectifier Diode [part_number=1N4001 package="300 mil [THT]"]
  R6 = Resistor [tolerance=±5% resistance=47k package=THT]
  R7 = Resistor [tolerance=±5% resistance=47k package=THT]
  R8 = Resistor [tolerance=±5% resistance=47k package=THT]
  J4 = Screw terminal - 2 pins [package=THT]
  J3 = Screw terminal - 2 pins [package=THT]
  J2 = Screw terminal - 2 pins [package=THT]
  J1 = Screw terminal - 2 pins [package=THT]
  J5 = Screw terminal - 2 pins [package=THT]
  J6 = Screw terminal - 2 pins [package=THT]
  C3 = Ceramic Capacitor [capacitance=100nF package="100 mil [THT, multilayer]"]
  C4 = Ceramic Capacitor [capacitance=100nF package="100 mil [THT, multilayer]"]
  C5 = Ceramic Capacitor [capacitance=100nF package="100 mil [THT, multilayer]"]
  C6 = Ceramic Capacitor [capacitance=100nF package="100 mil [THT, multilayer]"]

nets:
  GND: Part1.GND, U1.GND, C1.-, C2.1, R1.Pin_1, R2.Pin_1, R3.Pin_1, R4.Pin_1, J3.pin1, C3.0, C4.0, C5.1, C6.1
  N1: Part1.D2, R1.Pin_0, R5.Pin_1, C4.1
  N2: Part1.D3, R2.Pin_0, R6.Pin_1, C3.1
  N3: Part1.D4, R4.Pin_0, R8.Pin_1, C6.0
  N4: Part1.D5, R3.Pin_0, R7.Pin_1, C5.0
  N5: Part1.5V, U1.output_voltage, C1.+
  N6: Part1.A5, J4.pin1
  N7: Part1.A4, J4.pin2
  N8: U1.input_voltage, C2.0, J3.pin2
  N9: R5.Pin_0, D1.anode, J2.pin1
  N10: D1.cathode, D2.cathode, D3.cathode, D4.cathode, J6.pin2
  N11: D2.anode, R6.Pin_0, J2.pin2
  N12: D3.anode, R7.Pin_0, J1.pin1
  N13: D4.anode, R8.Pin_0, J1.pin2
  N14: J5.pin2, J6.pin1

notes:
  24 V ind
  24 V ud
  omskifter COM
  omskifter A
  omskifter B
  omskifter C
  omskifter D
  + 12 V
  GND
  I2C
  I2C SCL
  I2C SDA
